# Fritzing sketch Bluetooth car (saved by Fritzing 0.9.4)

parts:
  M1 = STM32F103C8T6 blue mini board
  L298N1 = L298N DC motor driver
  BAT1 = BC9VPC [package=bc9vpc]
  M2 = DC Motor
  M3 = DC Motor
  OLED_I2C1 = OLED 128x64 I2C Monochrome Display
  元件1 = Bluetooth HC-05 Macho

nets:
  N1: M1.B14, L298N1.IN4
  N2: M1.B15, L298N1.IN3
  N3: M1.A8, L298N1.IN2
  N4: M1.A9, L298N1.IN1
  N5: M1.B6, 元件1.RXD
  N6: M1.B7, 元件1.TXD
  N7: M1.B8, OLED_I2C1.SCK
  N8: M1.B9, OLED_I2C1.SDA
  5V: M1.5V, L298N1.5V
  GND: M1.G, M1.GND, L298N1.GND, BAT1.V-, OLED_I2C1.GND, 元件1.GND
  3.3V: M1.3.3V, OLED_I2C1.VDD, 元件1.VCC
  N9: M1.A0, L298N1.ENA
  N10: M1.A7, L298N1.ENB
  N11: L298N1.OUT1, M3.pin_2
  N12: L298N1.OUT2, M3.pin_1
  N13: L298N1.OUT3, M2.pin_2
  N14: L298N1.OUT4, M2.pin_1
  N15: L298N1.12V, BAT1.V+

custom parts:
  STM32F103C8T6 blue mini board: Generic Blue Pill microcomputer module, available from Ebay and others. CPU STM32F103C8 72Mhz Flash: 64 KB/128 KB RAM: 20KB.
  L298N DC motor driver: 2x DC motor driver with 78M05 positive voltage regulator (7..35 V) L298N: max 46 V, 2 A Set 5 V Enable jumper to enable 5 V regultor (needed for the L298N) and +5 V output at screw terminal or supply external +5 V at screw terminal Set ENA and/or ENB to +5 V to enable motor permanently or supply ENA and/or ENB with PWM signal IN1 and IN2 set rotation directory for motor A (OUT1/OUT2) IN2 and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
  DC Motor: Your standard DC Motor
